# Fritzing sketch wiring (saved by Fritzing 0.9.2b)
breadboards: 1

parts:
  パーツ2 = Arduino Wireless SD Shield
  J1 = Basic Servo
  S6 = Pushbutton [package="[THT]"]
  LED2 = LED - 5mm [color="Green (565nm)" package="5 mm [THT]"]
  LED3 = LED - 5mm [color="Red (633nm)" package="5 mm [THT]"]
  R2 = Temperature Sensor (Thermistor) [thermistor_type=NTC package=THT]
  R3 = Resistor [tolerance=±5% resistance=10k package=THT]
  R4 = Rotary Potentiometer (Small) [maximum_resistance=100kΩ package=THT]

nets:
  N1: パーツ2.A0, R2.pin_1, R3.Pin_1
  N2: パーツ2.A1, R4.wiper
  N3: パーツ2.D9, S6.Pin_1, S6.Pin_2
  N4: パーツ2.D10, J1.pulse
  N5: パーツ2.D2, LED3.anode
  N6: パーツ2.D3, LED2.anode
  +5V: パーツ2.+5V, J1.vcc, R2.pin_0, R4.leg2
  GND: パーツ2.GND, J1.gnd, S6.Pin_3, S6.Pin_4, LED2.cathode, LED3.cathode, R3.Pin_0, R4.leg1
